# Fritzing sketch 04-humedad (saved by Fritzing 0.9.3b)
breadboards: 1

parts:
  WeMos_D1_R1 = WeMos D1 R2
  LED1 = LED - 3mm [color="Green (555nm)" package="3 mm [THT]"]
  LED2 = LED - 3mm [color="Yellow (595nm)" package="3 mm [THT]"]
  LED3 = LED - 3mm [color="Red (633nm)" package="3 mm [THT]"]
  hc-sr1 = hc-sr04
  DHT1 = DHT11 Humitidy and Temperature Sensor  # not connected

nets:
  N1: WeMos_D1_R1.D1/TX, hc-sr1.Trig
  N2: WeMos_D1_R1.D2, hc-sr1.Echo
  N3: WeMos_D1_R1.(D6), LED3.anode
  GND: WeMos_D1_R1.D8, WeMos_D1_R1.GND, LED1.cathode, LED2.cathode, LED3.cathode, hc-sr1.GND
  5V: WeMos_D1_R1.5V, hc-sr1.VCC

custom parts:
  WeMos D1 R2: The D1 R2 is a mini wifi board based on the ESP-8266EX.
  DHT11 Humitidy and Temperature Sensor: DHT11 Humidity and Temperature Sensor
